// Digital circuit ID-OP.dig as structural Verilog
module ID_OP (
  input  clk,
  input  str,
  input  ldr,
  input  [1:0] DMUX,
  input  [1:0] ALUOP,
  input  [7:0] imm8,
  input  [2:0] WS,
  input  WE,
  input  FE,
  input  [15:0] ResultRefer,
  input  [2:0] RS1,
  input  [2:0] RS2,
  input  [15:0] R1,
  input  [15:0] R2,
  input  [4:0] RErefer,
  input  cond,
  input  [3:0] Frefer,
  output [15:0] _1,
  output [15:0] _2,
  output [5:0] ctr,
  output [7:0] imm8out,
  output [4:0] R,
  output FlushSignal
);

  wire doNothing, LDR_t, not_1_out, not_2_out, STR_t, WE_t;
  wire [2:0] xnor_1_out, xnor_2_out;
  wire [15:0] multiplexer_1_out, multiplexer_2_out;

  not not_1 (not_1_out, Frefer[0]);
  not not_2 (not_2_out, doNothing);
  and and_1 (doNothing, not_1_out, cond);
  and and_2 (WE_t, WE, not_2_out);
  and and_3 (STR_t, str, not_2_out);
  and and_4 (LDR_t, ldr, not_2_out);
  // Probe on RErefer[2:0]
  // Probe on RS1
  assign xnor_1_out = ~(RS1 ^ RErefer[2:0]);  // XNOr xnor_1, 3 bits wide
  // Probe on ResultRefer
  Multiplexer #(.Selector_Bits(3), .Bits(16)) multiplexer_1 (
    .sel(xnor_1_out), .in_0(R1), .in_1(R1), .in_2(R1), .in_3(R1), .in_4(R1), .in_5(R1), .in_6(R1),
    .in_7(ResultRefer), .out(multiplexer_1_out));
  assign xnor_2_out = ~(RErefer[2:0] ^ RS2);  // XNOr xnor_2, 3 bits wide
  Multiplexer #(.Selector_Bits(3), .Bits(16)) multiplexer_2 (
    .sel(xnor_2_out), .in_0(R2), .in_1(R2), .in_2(R2), .in_3(R2), .in_4(R2), .in_5(R2), .in_6(R2),
    .in_7(ResultRefer), .out(multiplexer_2_out));
  and and_5 (FlushSignal, WS[0], WS[1], WS[2]);
  Register #(.Bits(16)) register_1 (.D(multiplexer_1_out), .C(clk), .en(1'b1), .Q(_1));
  Register #(.Bits(16)) register_2 (.D(multiplexer_2_out), .C(clk), .en(1'b1), .Q(_2));
  Register #(.Bits(5)) registerEnable (.D({FE, WE_t, WS}), .C(clk), .en(1'b1), .Q(R));
  Register #(.Bits(6)) register_3 (.D({DMUX, ALUOP, LDR_t, STR_t}), .C(clk), .en(1'b1), .Q(ctr));
  Register #(.Bits(8)) register_4 (.D(imm8), .C(clk), .en(1'b1), .Q(imm8out));
endmodule

/* Test case refer:
RS1 RS2 R1 R2 ResultRefer RErefer 1 2

001 010 0x1000 0x1001 0xffff 00001 0xffff 0x1001
001 010 0x1000 0x1001 0xffff 00010 0x1000 0xffff
*/

/* Test case flush:
WS FlushSignal
111 1
110 0
*/
