// Digital circuit IF-ID.dig as structural Verilog
module IF_ID (
  input  [15:0] inst,
  input  clk,
  input  flushin,
  output [15:0] inst_out
);

  wire [15:0] multiplexer_1_out;

  Multiplexer #(.Bits(16)) multiplexer_1 (.sel(flushin), .in_0(inst), .in_1({16{1'b0}}), .out(multiplexer_1_out));
  Register #(.Bits(16)) _16 (.D(multiplexer_1_out), .C(clk), .en(1'b1), .Q(inst_out));
endmodule
