// Digital circuit OP-WB.dig as structural Verilog
module OP_WB (
  input  [15:0] Opresult,
  input  clk,
  input  [4:0] RE_2,
  input  [3:0] Flag,
  output [15:0] resultO,
  output [4:0] re,
  output [3:0] flagO,
  output FlushSignal
);

  Register #(.Bits(16)) register_1 (.D(Opresult), .C(clk), .en(1'b1), .Q(resultO));
  Register #(.Bits(4)) register_2 (.D(Flag), .C(clk), .en(1'b1), .Q(flagO));
  Register #(.Bits(5)) register_3 (.D(RE_2), .C(clk), .en(1'b1), .Q(re));
  and and_1 (FlushSignal, RE_2[0], RE_2[1], RE_2[2]);
endmodule
