// Digital circuit control_unit.dig as structural Verilog
module control_unit (
  input  [15:0] INST,
  input  [15:0] Flagin,
  output [1:0] ALUOP,
  output [2:0] RS1,
  output [2:0] RS2,
  output [2:0] WS,
  output STR,
  output WE,
  output [1:0] DMUX,
  output LDR,
  output FLEN,
  output cond
);

  wire doNothing, not_1_out, not_3_out, not_4_out, not_5_out;
  wire [0:0] not_2_out;
  wire [1:0] multiplexer_2_out;

  not not_1 (not_1_out, Flagin[0]);
  and and_1 (doNothing, not_1_out, INST[11]);
  Multiplexer #(.Bits(3)) multiplexer_1 (.sel(not_3_out), .in_0(INST[10:8]), .in_1(INST[2:0]), .out(RS2));
  not not_2 (not_2_out[0], INST[12]);
  not not_3 (not_3_out, multiplexer_2_out[0]);
  Multiplexer #(.Selector_Bits(2), .Bits(2)) multiplexer_2 (
    .sel(INST[15:14]), .in_0(2'b00), .in_1({INST[12], not_2_out[0]}), .in_2(2'b00), .in_3(2'b00),
    .out(multiplexer_2_out));
  not not_4 (not_4_out, multiplexer_2_out[0]);
  not not_5 (not_5_out, doNothing);
  Multiplexer #(.Selector_Bits(2), .Bits(2)) multiplexer_3 (
    .sel(INST[15:14]), .in_0({1'b1, INST[12]}), .in_1(INST[15:14]), .in_2(2'b00), .in_3(2'b00), .out(DMUX));
  and and_2 (WE, not_4_out, not_5_out);
  and and_3 (STR, multiplexer_2_out[0], not_5_out);
  and and_4 (LDR, multiplexer_2_out[1], not_5_out);
  nor nor_1 (FLEN, DMUX[0], DMUX[1]);
  Multiplexer #(.Selector_Bits(2), .Bits(3)) multiplexer_4 (
    .sel(DMUX), .in_0(INST[6:4]), .in_1(INST[6:4]), .in_2(INST[6:4]), .in_3(INST[10:8]), .out(RS1));

  assign ALUOP = INST[13:12];
  assign cond = INST[11];
  assign WS = INST[10:8];

  // Other names for the same wires on the sheet: primeRS1[2:0] = INST[6:4]; RD[2:0] = INST[10:8]; firstBit = INST[12]

  // Notes on the sheet:
  //   cond
  //   Rd
  //   Ra
  //   Rb
  //   opcode
endmodule

/* Test case All Tests:
	INST                                    WE  ALUOP  RS1   RS2  WS  STR  LDR DMUX

let aluop  = 0b1000;
let ldrop  = 0b0101;
let strop  = 0b0100;
let movlop = 0b0000;

loop(rd, 1<<3)
loop(ra, 1<<3)
loop(rb, 1<<3)

loop(i, 4)
	((aluop+i)<<12 | rd<<8 | ra<<4 | rb<<0) 1  (i)     (ra)  (rb) (rd)  0   X    0  #test add/sub/and/orr
end loop

	(ldrop    <<12 | rd<<8 | ra<<4 )        1  X       (ra)  x    (rd)  0   1    1  #test ldr
	(strop    <<12 | rd<<8 | ra<<4 )        0  X       (ra)  (rd)  X    1   X    X  #test str
	
	let imm = random(256);
	(movlop   <<12 | rd<<8 | imm )          1  X       X      X   (rd)  0   X    2  #test movl

end loop
end loop
end loop
*/

/* Test case WS:
	INST                                    WS 

let aluop  = 0b1000;
let ldrop  = 0b0101;
let strop  = 0b0100;
let movlop = 0b0000;

loop(rd, 1<<3)
loop(ra, 1<<3)
loop(rb, 1<<3)

loop(i, 4)
	((aluop+i)<<12 | rd<<8 | ra<<4 | rb<<0) (rd)  #test add/sub/and/orr
end loop

	(ldrop    <<12 | rd<<8 | ra<<4 )        (rd)   #test ldr
	(strop    <<12 | rd<<8 | ra<<4 )        X     #test str
	
	let imm = random(256);
	(movlop   <<12 | rd<<8 | imm )          (rd)  #test movl

end loop
end loop
end loop
*/

/* Test case RS1:
	INST                                    RS1  

let aluop  = 0b1000;
let ldrop  = 0b0101;
let strop  = 0b0100;
let movlop = 0b0000;

loop(rd, 1<<3)
loop(ra, 1<<3)
loop(rb, 1<<3)

loop(i, 4)
	((aluop+i)<<12 | rd<<8 | ra<<4 | rb<<0) (ra)  #test add/sub/and/orr
end loop

	(ldrop    <<12 | rd<<8 | ra<<4 )        (ra)  #test ldr
	(strop    <<12 | rd<<8 | ra<<4 )        (ra)  #test str

end loop
end loop
end loop
*/

/* Test case RS2:
	INST                                    RS2  

let aluop  = 0b1000;
let ldrop  = 0b0101;
let strop  = 0b0100;
let movlop = 0b0000;

loop(rd, 1<<3)
loop(ra, 1<<3)
loop(rb, 1<<3)

loop(i, 4)
	((aluop+i)<<12 | rd<<8 | ra<<4 | rb<<0) (rb) #test add/sub/and/orr
end loop
	(strop    <<12 | rd<<8 | ra<<4 )        (rd) #test str

end loop
end loop
end loop
*/

/* Test case STR:
	INST                                    STR 

let aluop  = 0b1000;
let ldrop  = 0b0101;
let strop  = 0b0100;
let movlop = 0b0000;

loop(rd, 1<<3)
loop(ra, 1<<3)
loop(rb, 1<<3)

loop(i, 4)
	((aluop+i)<<12 | rd<<8 | ra<<4 | rb<<0) 0  #test add/sub/and/orr
end loop

	(ldrop    <<12 | rd<<8 | ra<<4 )        0  #test ldr
	(strop    <<12 | rd<<8 | ra<<4 )        1  #test str
	
	let imm = random(256);
	(movlop   <<12 | rd<<8 | imm )          0  #test movl

end loop
end loop
end loop
*/

/* Test case WE:
	INST                                    WE  

let aluop  = 0b1000;
let ldrop  = 0b0101;
let strop  = 0b0100;
let movlop = 0b0000;

loop(rd, 1<<3)
loop(ra, 1<<3)
loop(rb, 1<<3)

loop(i, 4)
	((aluop+i)<<12 | rd<<8 | ra<<4 | rb<<0) 1  #test add/sub/and/orr
end loop

	(ldrop    <<12 | rd<<8 | ra<<4 )        1  #test ldr
	(strop    <<12 | rd<<8 | ra<<4 )        0  #test str
	
	let imm = random(256);
	(movlop   <<12 | rd<<8 | imm )          1  #test movl

end loop
end loop
end loop
*/

/* Test case LDR:
	INST                                    LDR 

let aluop  = 0b1000;
let ldrop  = 0b0101;
let strop  = 0b0100;
let movlop = 0b0000;

loop(rd, 1<<3)
loop(ra, 1<<3)
loop(rb, 1<<3)

loop(i, 4)
	((aluop+i)<<12 | rd<<8 | ra<<4 | rb<<0) X    #test add/sub/and/orr
end loop

	(ldrop    <<12 | rd<<8 | ra<<4 )        1    #test ldr
	(strop    <<12 | rd<<8 | ra<<4 )        X    #test str
	
	let imm = random(256);
	(movlop   <<12 | rd<<8 | imm )          X    #test movl

end loop
end loop
end loop
*/

/* Test case DMUX:
	INST                                    DMUX

let aluop  = 0b1000;
let ldrop  = 0b0101;
let strop  = 0b0100;
let movlop = 0b0000;

loop(rd, 1<<3)
loop(ra, 1<<3)
loop(rb, 1<<3)

loop(i, 4)
	((aluop+i)<<12 | rd<<8 | ra<<4 | rb<<0) 0  #test add/sub/and/orr
end loop

	(ldrop    <<12 | rd<<8 | ra<<4 )        1  #test ldr
	
	let imm = random(256);
	(movlop   <<12 | rd<<8 | imm )          2  #test movl

end loop
end loop
end loop
*/

/* Test case ALUOP:
	INST                                    ALUOP 

let aluop  = 0b1000;
let ldrop  = 0b0101;
let strop  = 0b0100;
let movlop = 0b0000;

loop(rd, 1<<3)
loop(ra, 1<<3)
loop(rb, 1<<3)

loop(i, 4)
	((aluop+i)<<12 | rd<<8 | ra<<4 | rb<<0) (i)    #test add/sub/and/orr
end loop

end loop
end loop
end loop
*/
