// Digital circuit pipelinedCPU.dig as structural Verilog
module pipelinedCPU (
  input  CLK
);

  wire control_unit_1_cond, control_unit_1_flen, control_unit_1_ldr, control_unit_1_str, control_unit_1_we,
       FLEN, id_op_1_flushsignal, LDR, op_wb_1_flushsignal, or_1_out, STR, WE;
  wire [1:0] control_unit_1_aluop, control_unit_1_dmux, id_op_1_ctr;
  wire [2:0] control_unit_1_rs1, control_unit_1_rs2, control_unit_1_ws, WS;
  wire [3:0] alu_1_flag, FLAGin;
  wire [4:0] id_op_1_r;
  wire [5:4] id_op_1_ctr_2;
  wire [7:0] id_op_1_imm8out, imm8;
  wire [15:0] _1D, alu_1_result, multiplexer_1_out, OPInfo, ra, RAM_d2, rb, reg_file_1_flagout,
       reg_file_1_out1, reg_file_1_out2, reg_file_1_pcout, seth_1_result;
  wire [15:8] if_id_1_inst_out;

  RAMDualAccess #(.AddrBits(16), .isProgramMemory("true"), .Bits(16)) RAM (
    .str(STR), .C(CLK), .ld(LDR), .A1(ra), .Din1(rb), .A2(reg_file_1_pcout), .D1(_1D), .D2(RAM_d2));
  IF_ID if_id_1 (.inst(RAM_d2), .clk(CLK), .flushin(or_1_out), .inst_out({if_id_1_inst_out, imm8}));
  // Probe inst on {if_id_1_inst_out, imm8}
  control_unit control_unit_1 (
    .INST({if_id_1_inst_out, imm8}), .Flagin(reg_file_1_flagout), .ALUOP(control_unit_1_aluop),
    .RS1(control_unit_1_rs1), .RS2(control_unit_1_rs2), .WS(control_unit_1_ws), .STR(control_unit_1_str),
    .WE(control_unit_1_we), .DMUX(control_unit_1_dmux), .LDR(control_unit_1_ldr), .FLEN(control_unit_1_flen),
    .cond(control_unit_1_cond));
  // Probe rs2 on control_unit_1_rs2
  // Probe rs1 on control_unit_1_rs1
  reg_file reg_file_1 (
    .WS(WS), .WE(WE), .IN(OPInfo), .clk(CLK), .RS1(control_unit_1_rs1), .RS2(control_unit_1_rs2),
    .FLAGin({{12{1'b0}}, FLAGin}), .FLEN(FLEN), .OUT1(reg_file_1_out1), .OUT2(reg_file_1_out2),
    .FLAGout(reg_file_1_flagout), .PCout(reg_file_1_pcout));
  // Probe flag on reg_file_1_flagout
  // Probe rf1 on reg_file_1_out1
  // Probe rf2 on reg_file_1_out2
  // Probe on control_unit_1_we
  ID_OP id_op_1 (
    .clk(CLK), .str(control_unit_1_str), .ldr(control_unit_1_ldr), .DMUX(control_unit_1_dmux),
    .ALUOP(control_unit_1_aluop), .imm8(imm8), .WS(control_unit_1_ws), .WE(control_unit_1_we),
    .FE(control_unit_1_flen), .ResultRefer(multiplexer_1_out), .RS1(control_unit_1_rs1),
    .RS2(control_unit_1_rs2), .R1(reg_file_1_out1), .R2(reg_file_1_out2), .RErefer(id_op_1_r),
    .cond(control_unit_1_cond), .Frefer(alu_1_flag), ._1(ra), ._2(rb),
    .ctr({id_op_1_ctr_2, id_op_1_ctr, LDR, STR}), .imm8out(id_op_1_imm8out), .R(id_op_1_r),
    .FlushSignal(id_op_1_flushsignal));
  or or_1 (or_1_out, op_wb_1_flushsignal, id_op_1_flushsignal);
  // Probe r1 on ra
  // Probe r2 on rb
  alu alu_1 (.A(ra), .B(rb), .ALUOP(id_op_1_ctr), .RESULT(alu_1_result), .FLAG(alu_1_flag));
  // Probe on id_op_1_r[2:0]
  // Probe on id_op_1_r[3]
  // Probe on id_op_1_r[4]
  // Probe aluR on alu_1_result
  seth seth_1 (.imm8(id_op_1_imm8out), .RDvalue(ra), .result(seth_1_result));
  // Probe dmux on id_op_1_ctr_2
  Multiplexer #(.Selector_Bits(2), .Bits(16)) multiplexer_1 (
    .sel(id_op_1_ctr_2), .in_0(alu_1_result), .in_1(_1D), .in_2({{8{1'b0}}, id_op_1_imm8out}),
    .in_3(seth_1_result), .out(multiplexer_1_out));
  // Probe OP result on multiplexer_1_out
  OP_WB op_wb_1 (
    .Opresult(multiplexer_1_out), .clk(CLK), .RE_2(id_op_1_r), .Flag(alu_1_flag), .resultO(OPInfo),
    .re({FLEN, WE, WS}), .flagO(FLAGin), .FlushSignal(op_wb_1_flushsignal));
  // Probe on WS

  // Notes on the sheet:
  //   Fetch
  //   Decode
  //   &Register
  //   Operations
  //   WriteBack
endmodule

/* Test case movl:
CLK     R1     R2     R3     R4     PC
0        x      x      x      x 0x0000
c   0x000a      x      x      x 0x0001
c   0x000a 0x000b      x      x 0x0002
c   0x000a 0x000b 0x000c      x 0x0003
c   0x000a 0x000b 0x000c 0x000d 0x0004

program(0x010a,0x020b,0x030c,0x040d)
*/

/* Test case readable flags:
CLK     R1     R2     R3     R4   FLAG     PC

declare FLAG = FL & 0xF;

0        x      x      x      x      x 0x0000
loop(i, 4)
c        x      x      x      x      x      x
end loop
c   0x0076 0x0000 0x0005 0x000f 0x0000 0x0005

program(0x0176,0x9211,0x8350,0x040f,0xa334)
*/

/* Test case alu:
CLK     R1     R2     R3     R4     PC
0        x      x      x      x 0x0000
c   0x001a      x      x      x 0x0001
c   0x001a 0x0000      x      x 0x0002
c   0x001a 0xf000      x      x 0x0003
c   0x001a 0xf000 0x00ff      x 0x0004
c   0x001a 0xf000 0xcdff      x 0x0005
c   0x001a 0xf000 0xcdff 0xf01a 0x0006
c   0x001a 0xf000 0xcdff 0x0000 0x0007
c   0x001a 0xf000 0xcdff 0x2201 0x0008
c   0x001a 0xf000 0xcdff 0xddff 0x0009
c   0x001a 0xf000 0xcdff 0x001a 0x000a
c   0x001a 0xf000 0xcdff 0x001a 0x000b
c   0x001a 0xf000 0xcdff 0xf01a 0x000c
c   0x001a 0xf000 0xcdff 0xf01a 0x000d
c   0x0000 0xf000 0xcdff 0xf01a 0x000e
c   0x0000 0xcdff 0xcdff 0xf01a 0x000f

program(0x011a,0x8200,0x12f0,0x03ff,0x13cd,0x8412,0xa421,0x9423,0x9432,0xa413,0xa431,0xb412,0xb012,0x8100,0x8230)
*/

/* Test case fib:
CLK     R1     R2     R3     R4   FLAG     PC

declare FLAG = FL & 0xF;

0        x      x      x      x      x 0x0000
c   0x0001      x      x      x      x 0x0001
c   0x0001 0x0000      x      x      x 0x0002
c   0x0001 0x0000 0x0019      x      x 0x0003
c   0x0001 0x0000 0x0019      x 0x0004 0x0004
c   0x0001 0x0000 0x0019      x 0x0004 0x0005
c   0x0001 0x0000 0x0019 0x0001 0x0000 0x0006
c   0x0000 0x0000 0x0019 0x0001 0x0001 0x0007
c   0x0000 0x0001 0x0019 0x0001 0x0000 0x0008
c   0x0000 0x0001 0x0019 0x0001 0x0000 0x0009
c   0x0000 0x0001 0x0018 0x0001 0x0004 0x000a
c   0x0000 0x0001 0x0018 0x0001 0x0004 0x0003
c   0x0000 0x0001 0x0018 0x0001 0x0004 0x0004
c   0x0000 0x0001 0x0018 0x0001 0x0004 0x0005
c   0x0000 0x0001 0x0018 0x0001 0x0000 0x0006
c   0x0001 0x0001 0x0018 0x0001 0x0000 0x0007
c   0x0001 0x0001 0x0018 0x0001 0x0000 0x0008
c   0x0001 0x0001 0x0018 0x0001 0x0000 0x0009
c   0x0001 0x0001 0x0017 0x0001 0x0004 0x000a
c   0x0001 0x0001 0x0017 0x0001 0x0004 0x0003
c   0x0001 0x0001 0x0017 0x0001 0x0004 0x0004
c   0x0001 0x0001 0x0017 0x0001 0x0004 0x0005
c   0x0001 0x0001 0x0017 0x0002 0x0000 0x0006
c   0x0001 0x0001 0x0017 0x0002 0x0000 0x0007
c   0x0001 0x0002 0x0017 0x0002 0x0000 0x0008
c   0x0001 0x0002 0x0017 0x0001 0x0000 0x0009
c   0x0001 0x0002 0x0016 0x0001 0x0004 0x000a
c   0x0001 0x0002 0x0016 0x0001 0x0004 0x0003
c   0x0001 0x0002 0x0016 0x0001 0x0004 0x0004
c   0x0001 0x0002 0x0016 0x0001 0x0004 0x0005
c   0x0001 0x0002 0x0016 0x0003 0x0000 0x0006
c   0x0002 0x0002 0x0016 0x0003 0x0000 0x0007
c   0x0002 0x0003 0x0016 0x0003 0x0000 0x0008
c   0x0002 0x0003 0x0016 0x0001 0x0000 0x0009
c   0x0002 0x0003 0x0015 0x0001 0x0004 0x000a
c   0x0002 0x0003 0x0015 0x0001 0x0004 0x0003
c   0x0002 0x0003 0x0015 0x0001 0x0004 0x0004
c   0x0002 0x0003 0x0015 0x0001 0x0004 0x0005
c   0x0002 0x0003 0x0015 0x0005 0x0000 0x0006
c   0x0003 0x0003 0x0015 0x0005 0x0000 0x0007
c   0x0003 0x0005 0x0015 0x0005 0x0000 0x0008
c   0x0003 0x0005 0x0015 0x0001 0x0000 0x0009
c   0x0003 0x0005 0x0014 0x0001 0x0004 0x000a
c   0x0003 0x0005 0x0014 0x0001 0x0004 0x0003
c   0x0003 0x0005 0x0014 0x0001 0x0004 0x0004
c   0x0003 0x0005 0x0014 0x0001 0x0004 0x0005
c   0x0003 0x0005 0x0014 0x0008 0x0000 0x0006
c   0x0005 0x0005 0x0014 0x0008 0x0000 0x0007
c   0x0005 0x0008 0x0014 0x0008 0x0000 0x0008
c   0x0005 0x0008 0x0014 0x0001 0x0000 0x0009
c   0x0005 0x0008 0x0013 0x0001 0x0004 0x000a
c   0x0005 0x0008 0x0013 0x0001 0x0004 0x0003
c   0x0005 0x0008 0x0013 0x0001 0x0004 0x0004
c   0x0005 0x0008 0x0013 0x0001 0x0004 0x0005
c   0x0005 0x0008 0x0013 0x000d 0x0000 0x0006
c   0x0008 0x0008 0x0013 0x000d 0x0000 0x0007
c   0x0008 0x000d 0x0013 0x000d 0x0000 0x0008
c   0x0008 0x000d 0x0013 0x0001 0x0000 0x0009
c   0x0008 0x000d 0x0012 0x0001 0x0004 0x000a
c   0x0008 0x000d 0x0012 0x0001 0x0004 0x0003
c   0x0008 0x000d 0x0012 0x0001 0x0004 0x0004
c   0x0008 0x000d 0x0012 0x0001 0x0004 0x0005
c   0x0008 0x000d 0x0012 0x0015 0x0000 0x0006
c   0x000d 0x000d 0x0012 0x0015 0x0000 0x0007
c   0x000d 0x0015 0x0012 0x0015 0x0000 0x0008
c   0x000d 0x0015 0x0012 0x0001 0x0000 0x0009
c   0x000d 0x0015 0x0011 0x0001 0x0004 0x000a
c   0x000d 0x0015 0x0011 0x0001 0x0004 0x0003
c   0x000d 0x0015 0x0011 0x0001 0x0004 0x0004
c   0x000d 0x0015 0x0011 0x0001 0x0004 0x0005
c   0x000d 0x0015 0x0011 0x0022 0x0000 0x0006
c   0x0015 0x0015 0x0011 0x0022 0x0000 0x0007
c   0x0015 0x0022 0x0011 0x0022 0x0000 0x0008
c   0x0015 0x0022 0x0011 0x0001 0x0000 0x0009
c   0x0015 0x0022 0x0010 0x0001 0x0004 0x000a
c   0x0015 0x0022 0x0010 0x0001 0x0004 0x0003
c   0x0015 0x0022 0x0010 0x0001 0x0004 0x0004
c   0x0015 0x0022 0x0010 0x0001 0x0004 0x0005
c   0x0015 0x0022 0x0010 0x0037 0x0000 0x0006
c   0x0022 0x0022 0x0010 0x0037 0x0000 0x0007
c   0x0022 0x0037 0x0010 0x0037 0x0000 0x0008
c   0x0022 0x0037 0x0010 0x0001 0x0000 0x0009
c   0x0022 0x0037 0x000f 0x0001 0x0004 0x000a
c   0x0022 0x0037 0x000f 0x0001 0x0004 0x0003
c   0x0022 0x0037 0x000f 0x0001 0x0004 0x0004
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*/

/* Test case seth:
CLK     R1     R2     R3     R4     PC
0        x      x      x      x 0x0000
c   0x00ad      x      x      x 0x0001
c   0xdead      x      x      x 0x0002
c   0xdead 0x000d      x      x 0x0003
c   0xdead 0xf00d      x      x 0x0004
c   0xdead 0xf00d 0x00ef      x 0x0005
c   0xdead 0xf00d 0xbeef      x 0x0006
c   0xdead 0xf00d 0xbeef 0x00ad 0x0007
c   0xdead 0xf00d 0xbeef 0x0bad 0x0008

program(0x01ad,0x11de,0x020d,0x12f0,0x03ef,0x13be,0x04ad,0x140b)
*/

/* Test case flags:
CLK     R1     R2     R3     R4   FLAG     PC

declare FLAG = FL & 0xF;

0        x      x      x      x      x 0x0000
c   0x0001      x      x      x      x 0x0001
c   0x0001 0x00ff      x      x      x 0x0002
c   0x0001 0xffff      x      x      x 0x0003
c   0x0001 0xffff 0x00fe      x      x 0x0004
c   0x0001 0xffff 0xfffe      x      x 0x0005
c   0x0001 0xffff 0xfffe 0x0000 0x0001 0x0006
c   0x0001 0xffff 0xfffe 0x0000 0x0005 0x0007
c   0x0001 0xffff 0xfffe 0x0000 0x0005 0x0008
c   0x0001 0xffff 0xfffe 0x0002 0x0000 0x0009
c   0x0001 0xffff 0xfffe 0xfffe 0x0006 0x000a
c   0x0001 0xffff 0xfffe 0xffff 0x0002 0x000b
c   0x0001 0x00ff 0xfffe 0xffff 0x0002 0x000c
c   0x0001 0x7fff 0xfffe 0xffff 0x0002 0x000d
c   0x0001 0x7fff 0x0000 0xffff 0x0002 0x000e
c   0x0001 0x7fff 0x8000 0xffff 0x0002 0x000f
c   0x0001 0x7fff 0x8000 0xffff 0x0002 0x0010
c   0x0001 0x7fff 0x8000 0x8001 0x0002 0x0011
c   0x0001 0x7fff 0x8000 0x7fff 0x000c 0x0012
c   0x0001 0x7fff 0x8000 0x7ffe 0x0004 0x0013
c   0x0001 0x7fff 0x8000 0x0001 0x000c 0x0014
c   0x0001 0x7fff 0x8000 0x8000 0x000a 0x0015

program(0x0101,0x02ff,0x12ff,0x03fe,0x13ff,0x8400,0x8412,0x9411,0x9412,0x8422,0x8431,0x02ff,0x127f,0x0300,0x1380,0x8423,0x8431,0x9431,0x9421,0x9432,0x8412)
*/

/* Test case recursion:
CLK     R1     R2     R3     R4   FLAG     PC

declare FLAG = FL & 0xF;

0        x      x      x      x      x 0x0000
c        x      x      x 0x0000 0x0001 0x0001
c   0x0020      x      x 0x0000 0x0001 0x0002
c   0x0020 0x0008      x 0x0000 0x0001 0x0003
c   0x0020 0x0008 0x0001 0x0000 0x0001 0x0004
c   0x0021 0x0008 0x0001 0x0000 0x0000 0x0005
c   0x0021 0x0008 0x0001 0xffff 0x0002 0x0006
c   0x0021 0x0008 0x001f 0xffff 0x0002 0x0007
c   0x0021 0x0008 0x001f 0xffff 0x0002 0x0008
c   0x0021 0x0008 0x001f 0xffff 0x0004 0x0009
c   0x0021 0x0008 0x001f 0xffff 0x0004 0x000a
c   0x0021 0x0008 0x0001 0xffff 0x0004 0x000b
c   0x0021 0x0008 0x0001 0xfffe 0x0006 0x000c
c   0x0021 0x0008 0x0001 0xfffe 0x0006 0x000d
c   0x000f 0x0008 0x0001 0xfffe 0x0006 0x000e
c   0x000f 0x0008 0x0001 0xfffd 0x0006 0x000f
c   0x000f 0x0008 0x0001 0xfffd 0x0006 0x0010
c   0x000f 0x0007 0x0001 0xfffd 0x0004 0x0011
c   0xfffe 0x0007 0x0001 0xfffd 0x0002 0x0012
c   0x0021 0x0007 0x0001 0xfffd 0x0002 0x0013
c   0x0022 0x0007 0x0001 0xfffd 0x0000 0x0014
c   0x0022 0x0007 0x0001 0xfffc 0x0006 0x0015
c   0x0022 0x0007 0x0018 0xfffc 0x0006 0x0016
c   0x0022 0x0007 0x0018 0xfffc 0x0006 0x0017
c   0x0022 0x0007 0x0018 0xfffc 0x0006 0x0008
c   0x0022 0x0007 0x0018 0xfffc 0x0004 0x0009
c   0x0022 0x0007 0x0018 0xfffc 0x0004 0x000a
c   0x0022 0x0007 0x0001 0xfffc 0x0004 0x000b
c   0x0022 0x0007 0x0001 0xfffb 0x0006 0x000c
c   0x0022 0x0007 0x0001 0xfffb 0x0006 0x000d
c   0x0004 0x0007 0x0001 0xfffb 0x0006 0x000e
c   0x0004 0x0007 0x0001 0xfffa 0x0006 0x000f
c   0x0004 0x0007 0x0001 0xfffa 0x0006 0x0010
c   0x0004 0x0006 0x0001 0xfffa 0x0004 0x0011
c   0xfffb 0x0006 0x0001 0xfffa 0x0002 0x0012
c   0x0022 0x0006 0x0001 0xfffa 0x0002 0x0013
c   0x0023 0x0006 0x0001 0xfffa 0x0000 0x0014
c   0x0023 0x0006 0x0001 0xfff9 0x0006 0x0015
c   0x0023 0x0006 0x0018 0xfff9 0x0006 0x0016
c   0x0023 0x0006 0x0018 0xfff9 0x0006 0x0017
c   0x0023 0x0006 0x0018 0xfff9 0x0006 0x0008
c   0x0023 0x0006 0x0018 0xfff9 0x0004 0x0009
c   0x0023 0x0006 0x0018 0xfff9 0x0004 0x000a
c   0x0023 0x0006 0x0001 0xfff9 0x0004 0x000b
c   0x0023 0x0006 0x0001 0xfff8 0x0006 0x000c
c   0x0023 0x0006 0x0001 0xfff8 0x0006 0x000d
c   0x0005 0x0006 0x0001 0xfff8 0x0006 0x000e
c   0x0005 0x0006 0x0001 0xfff7 0x0006 0x000f
c   0x0005 0x0006 0x0001 0xfff7 0x0006 0x0010
c   0x0005 0x0005 0x0001 0xfff7 0x0004 0x0011
c   0xfff8 0x0005 0x0001 0xfff7 0x0002 0x0012
c   0x0023 0x0005 0x0001 0xfff7 0x0002 0x0013
c   0x0024 0x0005 0x0001 0xfff7 0x0000 0x0014
c   0x0024 0x0005 0x0001 0xfff6 0x0006 0x0015
c   0x0024 0x0005 0x0018 0xfff6 0x0006 0x0016
c   0x0024 0x0005 0x0018 0xfff6 0x0006 0x0017
c   0x0024 0x0005 0x0018 0xfff6 0x0006 0x0008
c   0x0024 0x0005 0x0018 0xfff6 0x0004 0x0009
c   0x0024 0x0005 0x0018 0xfff6 0x0004 0x000a
c   0x0024 0x0005 0x0001 0xfff6 0x0004 0x000b
c   0x0024 0x0005 0x0001 0xfff5 0x0006 0x000c
c   0x0024 0x0005 0x0001 0xfff5 0x0006 0x000d
c   0x0006 0x0005 0x0001 0xfff5 0x0006 0x000e
c   0x0006 0x0005 0x0001 0xfff4 0x0006 0x000f
c   0x0006 0x0005 0x0001 0xfff4 0x0006 0x0010
c   0x0006 0x0004 0x0001 0xfff4 0x0004 0x0011
c   0xfff5 0x0004 0x0001 0xfff4 0x0002 0x0012
c   0x0024 0x0004 0x0001 0xfff4 0x0002 0x0013
c   0x0025 0x0004 0x0001 0xfff4 0x0000 0x0014
c   0x0025 0x0004 0x0001 0xfff3 0x0006 0x0015
c   0x0025 0x0004 0x0018 0xfff3 0x0006 0x0016
c   0x0025 0x0004 0x0018 0xfff3 0x0006 0x0017
c   0x0025 0x0004 0x0018 0xfff3 0x0006 0x0008
c   0x0025 0x0004 0x0018 0xfff3 0x0004 0x0009
c   0x0025 0x0004 0x0018 0xfff3 0x0004 0x000a
c   0x0025 0x0004 0x0001 0xfff3 0x0004 0x000b
c   0x0025 0x0004 0x0001 0xfff2 0x0006 0x000c
c   0x0025 0x0004 0x0001 0xfff2 0x0006 0x000d
c   0x0007 0x0004 0x0001 0xfff2 0x0006 0x000e
c   0x0007 0x0004 0x0001 0xfff1 0x0006 0x000f
c   0x0007 0x0004 0x0001 0xfff1 0x0006 0x0010
c   0x0007 0x0003 0x0001 0xfff1 0x0004 0x0011
c   0xfff2 0x0003 0x0001 0xfff1 0x0002 0x0012
c   0x0025 0x0003 0x0001 0xfff1 0x0002 0x0013
c   0x0026 0x0003 0x0001 0xfff1 0x0000 0x0014
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*/

/* Test case ldr:
CLK     R1     R2     R3     R4     PC
0        x      x      x      x 0x0000
c   0x0003      x      x      x 0x0001
c   0x0003 0x9876      x      x 0x0002

program(0x0103,0x5210,0x0000,0x9876)
*/

/* Test case gp pc:
CLK     R1     R2     R3     R4   FLAG     PC

declare FLAG = FL & 0xF;

0        x      x      x      x      x 0x0000
c   0x0005      x      x      x      x 0x0001
c   0x0005 0x0098      x      x      x 0x0002
c   0x0005 0x0002      x      x 0x0000 0x0003
c   0x0005 0x0002      x      x 0x0000 0x0005

program(0x0105,0x0298,0x8270,0x8710,0x03ff,0x0000)
*/

/* Test case cond:
CLK     R1     R2     R3     R4   FLAG     PC

declare FLAG = FL & 0xF;

0        x      x      x      x      x 0x0000
c   0x0000      x      x      x      x 0x0001
c   0x0000 0x0000      x      x      x 0x0002
c   0x0000 0x0000 0x001a      x      x 0x0003
c   0x0000 0x0000 0x001a 0x0001      x 0x0004
c   0x0000 0x0000 0x001a 0x0001 0x0001 0x0005
c   0x0000 0x0001 0x001a 0x0001 0x0000 0x0006
c   0x0000 0x0001 0x001a 0x0001 0x0000 0x0007
c   0x0000 0x0001 0x001a 0x0001 0x0004 0x0008
c   0x0000 0x0001 0x001a 0x0001 0x0004 0x0009
c   0x0000 0x0001 0x001a 0x0001 0x0005 0x000a
c   0x1337 0x0001 0x001a 0x0001 0x0005 0x000b
c   0x1337 0x0001 0x001b 0x0001 0x0000 0x000c
c   0x1337 0x0001 0x001b 0x0001 0x0000 0x000d
c   0x1337 0x0000 0x001b 0x0001 0x0000 0x000e
c   0x1337 0x0000 0x001b 0x0001 0x0005 0x000f
c   0x1337 0x0000 0x001b 0x0001 0x0005 0x0010
c   0x1337 0x1337 0x001b 0x0001 0x0005 0x0011
c   0x1337 0x1337 0x001b 0x0001 0x0004 0x0012
c   0x1337 0x1337 0x001b 0x0001 0x0004 0x0013
c   0x1337 0x1337 0x001b 0x0001 0x0005 0x0014
c   0x0051 0x1337 0x001b 0x0001 0x0005 0x0015
c   0x0051 0x1337 0x001b 0x0001 0x0004 0x0016
c   0x0051 0x1337 0x001b 0x0001 0x0004 0x0017
c   0x0051 0x1337 0x001b 0x0001 0x0005 0x0018
c   0x5151 0x1337 0x001b 0x0001 0x0005 0x0019

program(0x0100,0x0200,0x031a,0x0401,0x8000,0x8a04,0xb944,0x9040,0x5930,0x9000,0x5930,0x8334,0x4930,0x5230,0x9000,0x4930,0x5230,0x9040,0x0915,0x9000,0x0951,0x9040,0x1915,0x9000,0x1951,0x0000,0x1337)
*/

/* Test case str:
CLK     R1     R2     R3     R4     PC
0        x      x      x      x 0x0000
c   0x0005      x      x      x 0x0001
c   0x0005 0x00f5      x      x 0x0002
c   0x0005 0x00f5      x      x 0x0003
c   0x0005 0x00f5 0x00f5      x 0x0004

program(0x0105,0x02f5,0x4210,0x5310,0x0000,0x0000)
*/

/* Test case mem:
CLK     R1     R2     R3     R4   FLAG     PC

declare FLAG = FL & 0xF;

0        x      x      x      x      x 0x0000
c   0x000a      x      x      x      x 0x0001
c   0x000a      x      x      x 0x0005 0x0002
c   0x000a 0xba55      x      x 0x0005 0x0003
c   0x000a 0xba55 0xba55      x 0x0005 0x0004
c   0x000a 0xba55 0xba55 0x0005 0x0005 0x0005
c   0x000f 0xba55 0xba55 0x0005 0x0000 0x0006
c   0x000f 0xba5a 0xba55 0x0005 0x0002 0x0007
c   0x000f 0xba5a 0xba55 0x0005 0x0002 0x0008
c   0x000f 0xba5a 0xba55 0xba5a 0x0002 0x0009

program(0x010a,0x9000,0x5210,0x5310,0x0405,0x8114,0x8224,0x4210,0x5410,0x0000,0xba55)
*/

/* Test case jumps:
CLK     R1     R2     R3     R4   FLAG     PC

declare FLAG = FL & 0xF;

0        x      x      x      x      x 0x0000
c        x      x      x 0x0003      x 0x0001
c   0x0001      x      x 0x0003 0x0000 0x0002
c   0x0001      x      x 0x0003 0x0000 0x0005
c   0x0001      x 0x0003 0x0003 0x0000 0x0006
c   0x0001      x 0x0003 0x0003 0x0004 0x0003
c   0x0001 0x0003 0x0003 0x0003 0x0004 0x0004
c   0x0001 0x0003 0x0003 0x0003 0x0000 0x0007
c   0x0001 0x0003 0x0003 0x0009 0x0000 0x0008
c   0x0001 0x0003 0x0003 0x0009 0x0000 0x000a

program(0x0403,0x8170,0x8774,0x0203,0x8772,0x0303,0x9773,0x0409,0x8714,0x8770,0x0000)
*/

/* Test case add:
CLK     R1     R2     R3     R4     PC
0        x      x      x      x 0x0000
c   0x0087      x      x      x 0x0001
c   0x0087 0x0093      x      x 0x0002
c   0x0087 0x0093 0x011a      x 0x0003

program(0x0187,0x0293,0x8321)
*/

/* Test case sub:
CLK     R1     R2     R3     R4     PC
0        x      x      x      x 0x0000
c        x      x      x 0x0027 0x0001
c        x 0x0093      x 0x0027 0x0002
c   0xff94 0x0093      x 0x0027 0x0003

program(0x0427,0x0293,0x9142)
*/

/* Test case and:
CLK     R1     R2     R3     R4     PC
0        x      x      x      x 0x0000
c   0x00aa      x      x      x 0x0001
c   0x00aa      x 0x00cc      x 0x0002
c   0x00aa      x 0x00cc 0x0088 0x0003

program(0x01aa,0x03cc,0xa413)
*/

/* Test case orr:
CLK     R1     R2     R3     R4     PC
0        x      x      x      x 0x0000
c        x      x      x 0x00aa 0x0001
c        x      x 0x00cc 0x00aa 0x0002
c        x 0x00ee 0x00cc 0x00aa 0x0003

program(0x04aa,0x03cc,0xb243)
*/
