// Digital circuit cpu.dig as structural Verilog
module cpu (
  input  CLK
);

  wire control_unit_1_cond, FLEN, LDR, STR, WE;
  wire [1:0] ALUOP, DMUX;
  wire [2:0] RS1, RS2, WS;
  wire [3:0] FLAGin;
  wire [15:0] alu_1_result, FLAGout, INST, multiplexer_1_out, RAM_d1, reg_file_1_out1, reg_file_1_out2,
       reg_file_1_pcout, seth_1_result;

  control_unit control_unit_1 (
    .INST(INST), .Flagin(FLAGout), .ALUOP(ALUOP), .RS1(RS1), .RS2(RS2), .WS(WS), .STR(STR), .WE(WE),
    .DMUX(DMUX), .LDR(LDR), .FLEN(FLEN), .cond(control_unit_1_cond));
  // Probe on control_unit_1_cond
  // Probe dmux on DMUX
  Multiplexer #(.Selector_Bits(2), .Bits(16)) multiplexer_1 (
    .sel(DMUX), .in_0(alu_1_result), .in_1(RAM_d1), .in_2({{8{1'b0}}, INST[7:0]}), .in_3(seth_1_result),
    .out(multiplexer_1_out));
  // Probe inst on INST
  seth seth_1 (.imm8(INST[7:0]), .RDvalue(reg_file_1_out1), .result(seth_1_result));
  reg_file reg_file_1 (
    .WS(WS), .WE(WE), .IN(multiplexer_1_out), .clk(CLK), .RS1(RS1), .RS2(RS2), .FLAGin({{12{1'b0}}, FLAGin}),
    .FLEN(FLEN), .OUT1(reg_file_1_out1), .OUT2(reg_file_1_out2), .FLAGout(FLAGout), .PCout(reg_file_1_pcout));
  // Probe flag on FLAGout
  RAMDualAccess #(.AddrBits(16), .isProgramMemory("true"), .Bits(16)) RAM (
    .str(STR), .C(CLK), .ld(LDR), .A1(reg_file_1_out1), .Din1(reg_file_1_out2), .A2(reg_file_1_pcout),
    .D1(RAM_d1), .D2(INST));
  alu alu_1 (.A(reg_file_1_out1), .B(reg_file_1_out2), .ALUOP(ALUOP), .RESULT(alu_1_result), .FLAG(FLAGin));
endmodule

/* Test case movl:
CLK     R1     R2     R3     R4     PC
0        x      x      x      x 0x0000
c   0x000a      x      x      x 0x0001
c   0x000a 0x000b      x      x 0x0002
c   0x000a 0x000b 0x000c      x 0x0003
c   0x000a 0x000b 0x000c 0x000d 0x0004

program(0x010a,0x020b,0x030c,0x040d)
*/

/* Test case readable flags:
CLK     R1     R2     R3     R4   FLAG     PC

declare FLAG = FL & 0xF;

0        x      x      x      x      x 0x0000
loop(i, 4)
c        x      x      x      x      x      x
end loop
c   0x0076 0x0000 0x0005 0x000f 0x0000 0x0005

program(0x0176,0x9211,0x8350,0x040f,0xa334)
*/

/* Test case alu:
CLK     R1     R2     R3     R4     PC
0        x      x      x      x 0x0000
c   0x001a      x      x      x 0x0001
c   0x001a 0x0000      x      x 0x0002
c   0x001a 0xf000      x      x 0x0003
c   0x001a 0xf000 0x00ff      x 0x0004
c   0x001a 0xf000 0xcdff      x 0x0005
c   0x001a 0xf000 0xcdff 0xf01a 0x0006
c   0x001a 0xf000 0xcdff 0x0000 0x0007
c   0x001a 0xf000 0xcdff 0x2201 0x0008
c   0x001a 0xf000 0xcdff 0xddff 0x0009
c   0x001a 0xf000 0xcdff 0x001a 0x000a
c   0x001a 0xf000 0xcdff 0x001a 0x000b
c   0x001a 0xf000 0xcdff 0xf01a 0x000c
c   0x001a 0xf000 0xcdff 0xf01a 0x000d
c   0x0000 0xf000 0xcdff 0xf01a 0x000e
c   0x0000 0xcdff 0xcdff 0xf01a 0x000f

program(0x011a,0x8200,0x12f0,0x03ff,0x13cd,0x8412,0xa421,0x9423,0x9432,0xa413,0xa431,0xb412,0xb012,0x8100,0x8230)
*/

/* Test case fib:
CLK     R1     R2     R3     R4   FLAG     PC

declare FLAG = FL & 0xF;

0        x      x      x      x      x 0x0000
c   0x0001      x      x      x      x 0x0001
c   0x0001 0x0000      x      x      x 0x0002
c   0x0001 0x0000 0x0019      x      x 0x0003
c   0x0001 0x0000 0x0019      x 0x0004 0x0004
c   0x0001 0x0000 0x0019      x 0x0004 0x0005
c   0x0001 0x0000 0x0019 0x0001 0x0000 0x0006
c   0x0000 0x0000 0x0019 0x0001 0x0001 0x0007
c   0x0000 0x0001 0x0019 0x0001 0x0000 0x0008
c   0x0000 0x0001 0x0019 0x0001 0x0000 0x0009
c   0x0000 0x0001 0x0018 0x0001 0x0004 0x000a
c   0x0000 0x0001 0x0018 0x0001 0x0004 0x0003
c   0x0000 0x0001 0x0018 0x0001 0x0004 0x0004
c   0x0000 0x0001 0x0018 0x0001 0x0004 0x0005
c   0x0000 0x0001 0x0018 0x0001 0x0000 0x0006
c   0x0001 0x0001 0x0018 0x0001 0x0000 0x0007
c   0x0001 0x0001 0x0018 0x0001 0x0000 0x0008
c   0x0001 0x0001 0x0018 0x0001 0x0000 0x0009
c   0x0001 0x0001 0x0017 0x0001 0x0004 0x000a
c   0x0001 0x0001 0x0017 0x0001 0x0004 0x0003
c   0x0001 0x0001 0x0017 0x0001 0x0004 0x0004
c   0x0001 0x0001 0x0017 0x0001 0x0004 0x0005
c   0x0001 0x0001 0x0017 0x0002 0x0000 0x0006
c   0x0001 0x0001 0x0017 0x0002 0x0000 0x0007
c   0x0001 0x0002 0x0017 0x0002 0x0000 0x0008
c   0x0001 0x0002 0x0017 0x0001 0x0000 0x0009
c   0x0001 0x0002 0x0016 0x0001 0x0004 0x000a
c   0x0001 0x0002 0x0016 0x0001 0x0004 0x0003
c   0x0001 0x0002 0x0016 0x0001 0x0004 0x0004
c   0x0001 0x0002 0x0016 0x0001 0x0004 0x0005
c   0x0001 0x0002 0x0016 0x0003 0x0000 0x0006
c   0x0002 0x0002 0x0016 0x0003 0x0000 0x0007
c   0x0002 0x0003 0x0016 0x0003 0x0000 0x0008
c   0x0002 0x0003 0x0016 0x0001 0x0000 0x0009
c   0x0002 0x0003 0x0015 0x0001 0x0004 0x000a
c   0x0002 0x0003 0x0015 0x0001 0x0004 0x0003
c   0x0002 0x0003 0x0015 0x0001 0x0004 0x0004
c   0x0002 0x0003 0x0015 0x0001 0x0004 0x0005
c   0x0002 0x0003 0x0015 0x0005 0x0000 0x0006
c   0x0003 0x0003 0x0015 0x0005 0x0000 0x0007
c   0x0003 0x0005 0x0015 0x0005 0x0000 0x0008
c   0x0003 0x0005 0x0015 0x0001 0x0000 0x0009
c   0x0003 0x0005 0x0014 0x0001 0x0004 0x000a
c   0x0003 0x0005 0x0014 0x0001 0x0004 0x0003
c   0x0003 0x0005 0x0014 0x0001 0x0004 0x0004
c   0x0003 0x0005 0x0014 0x0001 0x0004 0x0005
c   0x0003 0x0005 0x0014 0x0008 0x0000 0x0006
c   0x0005 0x0005 0x0014 0x0008 0x0000 0x0007
c   0x0005 0x0008 0x0014 0x0008 0x0000 0x0008
c   0x0005 0x0008 0x0014 0x0001 0x0000 0x0009
c   0x0005 0x0008 0x0013 0x0001 0x0004 0x000a
c   0x0005 0x0008 0x0013 0x0001 0x0004 0x0003
c   0x0005 0x0008 0x0013 0x0001 0x0004 0x0004
c   0x0005 0x0008 0x0013 0x0001 0x0004 0x0005
c   0x0005 0x0008 0x0013 0x000d 0x0000 0x0006
c   0x0008 0x0008 0x0013 0x000d 0x0000 0x0007
c   0x0008 0x000d 0x0013 0x000d 0x0000 0x0008
c   0x0008 0x000d 0x0013 0x0001 0x0000 0x0009
c   0x0008 0x000d 0x0012 0x0001 0x0004 0x000a
c   0x0008 0x000d 0x0012 0x0001 0x0004 0x0003
c   0x0008 0x000d 0x0012 0x0001 0x0004 0x0004
c   0x0008 0x000d 0x0012 0x0001 0x0004 0x0005
c   0x0008 0x000d 0x0012 0x0015 0x0000 0x0006
c   0x000d 0x000d 0x0012 0x0015 0x0000 0x0007
c   0x000d 0x0015 0x0012 0x0015 0x0000 0x0008
c   0x000d 0x0015 0x0012 0x0001 0x0000 0x0009
c   0x000d 0x0015 0x0011 0x0001 0x0004 0x000a
c   0x000d 0x0015 0x0011 0x0001 0x0004 0x0003
c   0x000d 0x0015 0x0011 0x0001 0x0004 0x0004
c   0x000d 0x0015 0x0011 0x0001 0x0004 0x0005
c   0x000d 0x0015 0x0011 0x0022 0x0000 0x0006
c   0x0015 0x0015 0x0011 0x0022 0x0000 0x0007
c   0x0015 0x0022 0x0011 0x0022 0x0000 0x0008
c   0x0015 0x0022 0x0011 0x0001 0x0000 0x0009
c   0x0015 0x0022 0x0010 0x0001 0x0004 0x000a
c   0x0015 0x0022 0x0010 0x0001 0x0004 0x0003
c   0x0015 0x0022 0x0010 0x0001 0x0004 0x0004
c   0x0015 0x0022 0x0010 0x0001 0x0004 0x0005
c   0x0015 0x0022 0x0010 0x0037 0x0000 0x0006
c   0x0022 0x0022 0x0010 0x0037 0x0000 0x0007
c   0x0022 0x0037 0x0010 0x0037 0x0000 0x0008
c   0x0022 0x0037 0x0010 0x0001 0x0000 0x0009
c   0x0022 0x0037 0x000f 0x0001 0x0004 0x000a
c   0x0022 0x0037 0x000f 0x0001 0x0004 0x0003
c   0x0022 0x0037 0x000f 0x0001 0x0004 0x0004
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*/

/* Test case seth:
CLK     R1     R2     R3     R4     PC
0        x      x      x      x 0x0000
c   0x00ad      x      x      x 0x0001
c   0xdead      x      x      x 0x0002
c   0xdead 0x000d      x      x 0x0003
c   0xdead 0xf00d      x      x 0x0004
c   0xdead 0xf00d 0x00ef      x 0x0005
c   0xdead 0xf00d 0xbeef      x 0x0006
c   0xdead 0xf00d 0xbeef 0x00ad 0x0007
c   0xdead 0xf00d 0xbeef 0x0bad 0x0008

program(0x01ad,0x11de,0x020d,0x12f0,0x03ef,0x13be,0x04ad,0x140b)
*/

/* Test case flags:
CLK     R1     R2     R3     R4   FLAG     PC

declare FLAG = FL & 0xF;

0        x      x      x      x      x 0x0000
c   0x0001      x      x      x      x 0x0001
c   0x0001 0x00ff      x      x      x 0x0002
c   0x0001 0xffff      x      x      x 0x0003
c   0x0001 0xffff 0x00fe      x      x 0x0004
c   0x0001 0xffff 0xfffe      x      x 0x0005
c   0x0001 0xffff 0xfffe 0x0000 0x0001 0x0006
c   0x0001 0xffff 0xfffe 0x0000 0x0005 0x0007
c   0x0001 0xffff 0xfffe 0x0000 0x0005 0x0008
c   0x0001 0xffff 0xfffe 0x0002 0x0000 0x0009
c   0x0001 0xffff 0xfffe 0xfffe 0x0006 0x000a
c   0x0001 0xffff 0xfffe 0xffff 0x0002 0x000b
c   0x0001 0x00ff 0xfffe 0xffff 0x0002 0x000c
c   0x0001 0x7fff 0xfffe 0xffff 0x0002 0x000d
c   0x0001 0x7fff 0x0000 0xffff 0x0002 0x000e
c   0x0001 0x7fff 0x8000 0xffff 0x0002 0x000f
c   0x0001 0x7fff 0x8000 0xffff 0x0002 0x0010
c   0x0001 0x7fff 0x8000 0x8001 0x0002 0x0011
c   0x0001 0x7fff 0x8000 0x7fff 0x000c 0x0012
c   0x0001 0x7fff 0x8000 0x7ffe 0x0004 0x0013
c   0x0001 0x7fff 0x8000 0x0001 0x000c 0x0014
c   0x0001 0x7fff 0x8000 0x8000 0x000a 0x0015

program(0x0101,0x02ff,0x12ff,0x03fe,0x13ff,0x8400,0x8412,0x9411,0x9412,0x8422,0x8431,0x02ff,0x127f,0x0300,0x1380,0x8423,0x8431,0x9431,0x9421,0x9432,0x8412)
*/

/* Test case recursion:
CLK     R1     R2     R3     R4   FLAG     PC

declare FLAG = FL & 0xF;

0        x      x      x      x      x 0x0000
c        x      x      x 0x0000 0x0001 0x0001
c   0x0020      x      x 0x0000 0x0001 0x0002
c   0x0020 0x0008      x 0x0000 0x0001 0x0003
c   0x0020 0x0008 0x0001 0x0000 0x0001 0x0004
c   0x0021 0x0008 0x0001 0x0000 0x0000 0x0005
c   0x0021 0x0008 0x0001 0xffff 0x0002 0x0006
c   0x0021 0x0008 0x001f 0xffff 0x0002 0x0007
c   0x0021 0x0008 0x001f 0xffff 0x0002 0x0008
c   0x0021 0x0008 0x001f 0xffff 0x0004 0x0009
c   0x0021 0x0008 0x001f 0xffff 0x0004 0x000a
c   0x0021 0x0008 0x0001 0xffff 0x0004 0x000b
c   0x0021 0x0008 0x0001 0xfffe 0x0006 0x000c
c   0x0021 0x0008 0x0001 0xfffe 0x0006 0x000d
c   0x000f 0x0008 0x0001 0xfffe 0x0006 0x000e
c   0x000f 0x0008 0x0001 0xfffd 0x0006 0x000f
c   0x000f 0x0008 0x0001 0xfffd 0x0006 0x0010
c   0x000f 0x0007 0x0001 0xfffd 0x0004 0x0011
c   0xfffe 0x0007 0x0001 0xfffd 0x0002 0x0012
c   0x0021 0x0007 0x0001 0xfffd 0x0002 0x0013
c   0x0022 0x0007 0x0001 0xfffd 0x0000 0x0014
c   0x0022 0x0007 0x0001 0xfffc 0x0006 0x0015
c   0x0022 0x0007 0x0018 0xfffc 0x0006 0x0016
c   0x0022 0x0007 0x0018 0xfffc 0x0006 0x0017
c   0x0022 0x0007 0x0018 0xfffc 0x0006 0x0008
c   0x0022 0x0007 0x0018 0xfffc 0x0004 0x0009
c   0x0022 0x0007 0x0018 0xfffc 0x0004 0x000a
c   0x0022 0x0007 0x0001 0xfffc 0x0004 0x000b
c   0x0022 0x0007 0x0001 0xfffb 0x0006 0x000c
c   0x0022 0x0007 0x0001 0xfffb 0x0006 0x000d
c   0x0004 0x0007 0x0001 0xfffb 0x0006 0x000e
c   0x0004 0x0007 0x0001 0xfffa 0x0006 0x000f
c   0x0004 0x0007 0x0001 0xfffa 0x0006 0x0010
c   0x0004 0x0006 0x0001 0xfffa 0x0004 0x0011
c   0xfffb 0x0006 0x0001 0xfffa 0x0002 0x0012
c   0x0022 0x0006 0x0001 0xfffa 0x0002 0x0013
c   0x0023 0x0006 0x0001 0xfffa 0x0000 0x0014
c   0x0023 0x0006 0x0001 0xfff9 0x0006 0x0015
c   0x0023 0x0006 0x0018 0xfff9 0x0006 0x0016
c   0x0023 0x0006 0x0018 0xfff9 0x0006 0x0017
c   0x0023 0x0006 0x0018 0xfff9 0x0006 0x0008
c   0x0023 0x0006 0x0018 0xfff9 0x0004 0x0009
c   0x0023 0x0006 0x0018 0xfff9 0x0004 0x000a
c   0x0023 0x0006 0x0001 0xfff9 0x0004 0x000b
c   0x0023 0x0006 0x0001 0xfff8 0x0006 0x000c
c   0x0023 0x0006 0x0001 0xfff8 0x0006 0x000d
c   0x0005 0x0006 0x0001 0xfff8 0x0006 0x000e
c   0x0005 0x0006 0x0001 0xfff7 0x0006 0x000f
c   0x0005 0x0006 0x0001 0xfff7 0x0006 0x0010
c   0x0005 0x0005 0x0001 0xfff7 0x0004 0x0011
c   0xfff8 0x0005 0x0001 0xfff7 0x0002 0x0012
c   0x0023 0x0005 0x0001 0xfff7 0x0002 0x0013
c   0x0024 0x0005 0x0001 0xfff7 0x0000 0x0014
c   0x0024 0x0005 0x0001 0xfff6 0x0006 0x0015
c   0x0024 0x0005 0x0018 0xfff6 0x0006 0x0016
c   0x0024 0x0005 0x0018 0xfff6 0x0006 0x0017
c   0x0024 0x0005 0x0018 0xfff6 0x0006 0x0008
c   0x0024 0x0005 0x0018 0xfff6 0x0004 0x0009
c   0x0024 0x0005 0x0018 0xfff6 0x0004 0x000a
c   0x0024 0x0005 0x0001 0xfff6 0x0004 0x000b
c   0x0024 0x0005 0x0001 0xfff5 0x0006 0x000c
c   0x0024 0x0005 0x0001 0xfff5 0x0006 0x000d
c   0x0006 0x0005 0x0001 0xfff5 0x0006 0x000e
c   0x0006 0x0005 0x0001 0xfff4 0x0006 0x000f
c   0x0006 0x0005 0x0001 0xfff4 0x0006 0x0010
c   0x0006 0x0004 0x0001 0xfff4 0x0004 0x0011
c   0xfff5 0x0004 0x0001 0xfff4 0x0002 0x0012
c   0x0024 0x0004 0x0001 0xfff4 0x0002 0x0013
c   0x0025 0x0004 0x0001 0xfff4 0x0000 0x0014
c   0x0025 0x0004 0x0001 0xfff3 0x0006 0x0015
c   0x0025 0x0004 0x0018 0xfff3 0x0006 0x0016
c   0x0025 0x0004 0x0018 0xfff3 0x0006 0x0017
c   0x0025 0x0004 0x0018 0xfff3 0x0006 0x0008
c   0x0025 0x0004 0x0018 0xfff3 0x0004 0x0009
c   0x0025 0x0004 0x0018 0xfff3 0x0004 0x000a
c   0x0025 0x0004 0x0001 0xfff3 0x0004 0x000b
c   0x0025 0x0004 0x0001 0xfff2 0x0006 0x000c
c   0x0025 0x0004 0x0001 0xfff2 0x0006 0x000d
c   0x0007 0x0004 0x0001 0xfff2 0x0006 0x000e
c   0x0007 0x0004 0x0001 0xfff1 0x0006 0x000f
c   0x0007 0x0004 0x0001 0xfff1 0x0006 0x0010
c   0x0007 0x0003 0x0001 0xfff1 0x0004 0x0011
c   0xfff2 0x0003 0x0001 0xfff1 0x0002 0x0012
c   0x0025 0x0003 0x0001 0xfff1 0x0002 0x0013
c   0x0026 0x0003 0x0001 0xfff1 0x0000 0x0014
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*/

/* Test case ldr:
CLK     R1     R2     R3     R4     PC
0        x      x      x      x 0x0000
c   0x0003      x      x      x 0x0001
c   0x0003 0x9876      x      x 0x0002

program(0x0103,0x5210,0x0000,0x9876)
*/

/* Test case gp pc:
CLK     R1     R2     R3     R4   FLAG     PC

declare FLAG = FL & 0xF;

0        x      x      x      x      x 0x0000
c   0x0005      x      x      x      x 0x0001
c   0x0005 0x0098      x      x      x 0x0002
c   0x0005 0x0002      x      x 0x0000 0x0003
c   0x0005 0x0002      x      x 0x0000 0x0005

program(0x0105,0x0298,0x8270,0x8710,0x03ff,0x0000)
*/

/* Test case cond:
CLK     R1     R2     R3     R4   FLAG     PC

declare FLAG = FL & 0xF;

0        x      x      x      x      x 0x0000
c   0x0000      x      x      x      x 0x0001
c   0x0000 0x0000      x      x      x 0x0002
c   0x0000 0x0000 0x001a      x      x 0x0003
c   0x0000 0x0000 0x001a 0x0001      x 0x0004
c   0x0000 0x0000 0x001a 0x0001 0x0001 0x0005
c   0x0000 0x0001 0x001a 0x0001 0x0000 0x0006
c   0x0000 0x0001 0x001a 0x0001 0x0000 0x0007
c   0x0000 0x0001 0x001a 0x0001 0x0004 0x0008
c   0x0000 0x0001 0x001a 0x0001 0x0004 0x0009
c   0x0000 0x0001 0x001a 0x0001 0x0005 0x000a
c   0x1337 0x0001 0x001a 0x0001 0x0005 0x000b
c   0x1337 0x0001 0x001b 0x0001 0x0000 0x000c
c   0x1337 0x0001 0x001b 0x0001 0x0000 0x000d
c   0x1337 0x0000 0x001b 0x0001 0x0000 0x000e
c   0x1337 0x0000 0x001b 0x0001 0x0005 0x000f
c   0x1337 0x0000 0x001b 0x0001 0x0005 0x0010
c   0x1337 0x1337 0x001b 0x0001 0x0005 0x0011
c   0x1337 0x1337 0x001b 0x0001 0x0004 0x0012
c   0x1337 0x1337 0x001b 0x0001 0x0004 0x0013
c   0x1337 0x1337 0x001b 0x0001 0x0005 0x0014
c   0x0051 0x1337 0x001b 0x0001 0x0005 0x0015
c   0x0051 0x1337 0x001b 0x0001 0x0004 0x0016
c   0x0051 0x1337 0x001b 0x0001 0x0004 0x0017
c   0x0051 0x1337 0x001b 0x0001 0x0005 0x0018
c   0x5151 0x1337 0x001b 0x0001 0x0005 0x0019

program(0x0100,0x0200,0x031a,0x0401,0x8000,0x8a04,0xb944,0x9040,0x5930,0x9000,0x5930,0x8334,0x4930,0x5230,0x9000,0x4930,0x5230,0x9040,0x0915,0x9000,0x0951,0x9040,0x1915,0x9000,0x1951,0x0000,0x1337)
*/

/* Test case str:
CLK     R1     R2     R3     R4     PC
0        x      x      x      x 0x0000
c   0x0005      x      x      x 0x0001
c   0x0005 0x00f5      x      x 0x0002
c   0x0005 0x00f5      x      x 0x0003
c   0x0005 0x00f5 0x00f5      x 0x0004

program(0x0105,0x02f5,0x4210,0x5310,0x0000,0x0000)
*/

/* Test case mem:
CLK     R1     R2     R3     R4   FLAG     PC

declare FLAG = FL & 0xF;

0        x      x      x      x      x 0x0000
c   0x000a      x      x      x      x 0x0001
c   0x000a      x      x      x 0x0005 0x0002
c   0x000a 0xba55      x      x 0x0005 0x0003
c   0x000a 0xba55 0xba55      x 0x0005 0x0004
c   0x000a 0xba55 0xba55 0x0005 0x0005 0x0005
c   0x000f 0xba55 0xba55 0x0005 0x0000 0x0006
c   0x000f 0xba5a 0xba55 0x0005 0x0002 0x0007
c   0x000f 0xba5a 0xba55 0x0005 0x0002 0x0008
c   0x000f 0xba5a 0xba55 0xba5a 0x0002 0x0009

program(0x010a,0x9000,0x5210,0x5310,0x0405,0x8114,0x8224,0x4210,0x5410,0x0000,0xba55)
*/

/* Test case add:
CLK     R1     R2     R3     R4     PC
0        x      x      x      x 0x0000
c   0x0087      x      x      x 0x0001
c   0x0087 0x0093      x      x 0x0002
c   0x0087 0x0093 0x011a      x 0x0003

program(0x0187,0x0293,0x8321)
*/

/* Test case jumps:
CLK     R1     R2     R3     R4   FLAG     PC

declare FLAG = FL & 0xF;

0        x      x      x      x      x 0x0000
c        x      x      x 0x0003      x 0x0001
c   0x0001      x      x 0x0003 0x0000 0x0002
c   0x0001      x      x 0x0003 0x0000 0x0005
c   0x0001      x 0x0003 0x0003 0x0000 0x0006
c   0x0001      x 0x0003 0x0003 0x0004 0x0003
c   0x0001 0x0003 0x0003 0x0003 0x0004 0x0004
c   0x0001 0x0003 0x0003 0x0003 0x0000 0x0007
c   0x0001 0x0003 0x0003 0x0009 0x0000 0x0008
c   0x0001 0x0003 0x0003 0x0009 0x0000 0x000a

program(0x0403,0x8170,0x8774,0x0203,0x8772,0x0303,0x9773,0x0409,0x8714,0x8770,0x0000)
*/

/* Test case sub:
CLK     R1     R2     R3     R4     PC
0        x      x      x      x 0x0000
c        x      x      x 0x0027 0x0001
c        x 0x0093      x 0x0027 0x0002
c   0xff94 0x0093      x 0x0027 0x0003

program(0x0427,0x0293,0x9142)
*/

/* Test case and:
CLK     R1     R2     R3     R4     PC
0        x      x      x      x 0x0000
c   0x00aa      x      x      x 0x0001
c   0x00aa      x 0x00cc      x 0x0002
c   0x00aa      x 0x00cc 0x0088 0x0003

program(0x01aa,0x03cc,0xa413)
*/

/* Test case orr:
CLK     R1     R2     R3     R4     PC
0        x      x      x      x 0x0000
c        x      x      x 0x00aa 0x0001
c        x      x 0x00cc 0x00aa 0x0002
c        x 0x00ee 0x00cc 0x00aa 0x0003

program(0x04aa,0x03cc,0xb243)
*/
