// Digital circuit seth.dig as structural Verilog
module seth (
  input  [7:0] imm8,
  input  [15:0] RDvalue,
  output [15:0] result
);


  assign result = {imm8, RDvalue[7:0]};
endmodule

/* Test case seth:
RDvalue imm8 result

0x12 0x34 0x3412
0x2212 0x1234 0x3412
*/
